// Logisim project rakesh M.R.circ as structural Verilog: 1 circuit, main circuit main
module main (
  input  in_1,
  input  in_2,
  input  in_3,
  output out_4
);

  wire and_1_out, and_4_out, and_5_out, not_1_out, not_2_out, not_3_out, undriven;

  not not_1 (not_1_out, in_1);
  not not_2 (not_2_out, in_1);
  not not_3 (not_3_out, in_1);
  and and_1 (and_1_out, not_1_out, in_1);
  // AND_Gate and_2 has open pins: in0=not_1_out, in1=in_1, in2=not_3_out, out=open
  // AND_Gate and_3 has open pins: in0=undriven, out=open
  and and_4 (and_4_out, in_1, not_2_out, in_1);
  and and_5 (and_5_out, in_1, in_1, in_1);
  // OR_Gate or_1 has open pins: in0=and_1_out, in4=and_4_out, out=open

  assign in_2 = in_1;
  assign in_3 = in_1;
  assign out_4 = in_1;
endmodule
